# Fritzing sketch schematic (saved by Fritzing 0.9.10b)
breadboards: 1

parts:
  M1 = Stepper Motor - Bipolar
  M2 = Stepper Motor - Bipolar
  Pololu_A1 = Pololu A4988 [package=SO16]
  Pololu_A2 = Pololu A4988 [package=SO16]
  C1 = Tantalum Capacitor [capacitance="1 μF" voltage=35V package="B 3528 [SMD, tantalum]"]
  C2 = Tantalum Capacitor [capacitance="1 μF" voltage=35V package="B 3528 [SMD, tantalum]"]
  Controller = Arduino Uno (Rev3)

nets:
  N1: M1.A, Pololu_A2.2B
  N2: M1.C, Pololu_A2.2A
  N3: M1.B, Pololu_A2.1A
  N4: M1.D, Pololu_A2.1B
  N5: M2.A, Pololu_A1.2B
  N6: M2.C, Pololu_A1.2A
  N7: M2.B, Pololu_A1.1A
  N8: M2.D, Pololu_A1.1B
  5V: Pololu_A1.MS1, Pololu_A1.MS2, Pololu_A1.MS3, Pololu_A1.VDD, Pololu_A2.MS1, Pololu_A2.MS2, Pololu_A2.MS3, Pololu_A2.VDD
  N9: Pololu_A1.RESET, Pololu_A1.SLEEP
  N10: Pololu_A1.STEP, Controller.D11_PWM/MOSI
  N11: Pololu_A1.DIR, Controller.D10_PWM/SS
  GND: Pololu_A1.GND, Pololu_A2.GND, C1.-, C2.-, Controller.GND
  12V: Pololu_A1.VMOT, Pololu_A2.VMOT, C1.+, C2.+
  N12: Pololu_A2.RESET, Pololu_A2.SLEEP
  N13: Pololu_A2.STEP, Controller.D9_PWM
  N14: Pololu_A2.DIR, Controller.D8
